// Logisim project Booth_multiplier.circ as structural Verilog: 1 circuit, main circuit main
module main (
  input  A0,
  input  A1,
  input  A2,
  input  A4,
  input  B0,
  input  B1,
  input  B2,
  input  B3,
  output S0,
  output S2,
  output S4,
  output S8,
  output S16,
  output S32,
  output S64,
  output S128
);

  wire adder_1_cout, adder_2_cout, adder_2_out, adder_3_cout, adder_3_out, adder_4_cout, adder_4_out,
       adder_5_cout, adder_6_cout, adder_6_out, adder_7_cout, adder_7_out, adder_8_cout, adder_8_out,
       adder_9_cout, adder_10_cout, adder_11_cout, and_2_out, and_3_out, and_4_out, and_5_out, and_6_out,
       and_7_out, and_8_out, and_9_out, and_10_out, and_11_out, and_12_out, and_13_out, and_14_out,
       and_15_out, and_16_out;

  and and_1 (S0, A0, B0);
  and and_2 (and_2_out, A1, B0);
  and and_3 (and_3_out, A0, B1);
  and and_4 (and_4_out, A0, B2);
  and and_5 (and_5_out, A1, B1);
  and and_6 (and_6_out, A2, B0);
  and and_7 (and_7_out, A0, B3);
  and and_8 (and_8_out, A1, B2);
  and and_9 (and_9_out, A2, B1);
  and and_10 (and_10_out, A4, B0);
  and and_11 (and_11_out, A1, B3);
  and and_12 (and_12_out, A2, B2);
  and and_13 (and_13_out, A4, B1);
  and and_14 (and_14_out, A2, B3);
  and and_15 (and_15_out, A4, B2);
  and and_16 (and_16_out, B3, A4);
  Adder #(.width(1)) adder_1 (.a(and_2_out), .b(and_3_out), .out(S2), .cout(adder_1_cout));  // open: cin
  Adder #(.width(1)) adder_2 (.a(and_4_out), .b(and_5_out), .out(adder_2_out), .cout(adder_2_cout));  // open: cin
  Adder #(.width(1)) adder_3 (.a(and_7_out), .b(and_8_out), .out(adder_3_out), .cout(adder_3_cout));  // open: cin
  Adder #(.width(1)) adder_4 (
    .a(and_11_out), .b(and_12_out), .out(adder_4_out), .cin(adder_3_cout), .cout(adder_4_cout));
  Adder #(.width(1)) adder_5 (.a(adder_2_out), .b(and_6_out), .out(S4), .cin(adder_1_cout), .cout(adder_5_cout));
  Adder #(.width(1)) adder_6 (
    .a(adder_3_out), .b(and_9_out), .out(adder_6_out), .cin(adder_2_cout), .cout(adder_6_cout));
  Adder #(.width(1)) adder_7 (
    .a(adder_4_out), .b(and_13_out), .out(adder_7_out), .cin(adder_6_cout), .cout(adder_7_cout));
  Adder #(.width(1)) adder_8 (
    .a(and_14_out), .b(and_15_out), .out(adder_8_out), .cin(adder_4_cout), .cout(adder_8_cout));
  Adder #(.width(1)) adder_9 (.a(adder_6_out), .b(and_10_out), .out(S8), .cin(adder_5_cout), .cout(adder_9_cout));
  Adder #(.width(1)) adder_10 (.a(adder_9_cout), .b(adder_7_out), .out(S16), .cout(adder_10_cout));  // open: cin
  Adder #(.width(1)) adder_11 (.a(adder_7_cout), .b(adder_8_out), .out(S32), .cin(adder_10_cout), .cout(adder_11_cout));
  Adder #(.width(1)) adder_12 (.a(adder_8_cout), .b(and_16_out), .out(S64), .cin(adder_11_cout), .cout(S128));

  // Notes on the sheet:
  //   4 bit Booth Multiplier
endmodule
